// Digital circuit CORE.dig as structural Verilog
module CORE (
  input  clk,
  input  RST,
  input  CLR,
  input  in_4,
  input  [11:0] MIPCBI,
  input  [15:0] PCBI,
  input  MIPCBE,
  input  PCBE
);

  wire ALUD_CO, ALUDH_OE, ALUDL_OE, ALUS_OE, and_3_out, and_4_out, and_5_out, ASSERT_f, BR_Q, button_1_out,
       CLK_t, CLKR, comparator_1_eq, comparator_1_gt, comparator_1_lt, comparator_2_eq, comparator_3_eq,
       DC_JUMP, DUMP_p5, EXT_p5, IMMED_OE, IRQ_OE, not_1_out, or_1_out, RAM_OE, RAM_WE, RF_HWE, RF_LWE,
       RF_SFR, RFSRCR_WE, ROM_OE, SFR_OE, SR_WE, WR_WE, XRAM_OE;
  wire [2:0] BR_SRC, BUS_SRC, JUMP_TYPE;
  wire [3:0] ALUSD_FUNC, multiplexer_2_out, RF_SRC;
  wire [5:4] multiplexer_2_out_2;
  wire [6:0] and_2_out;
  wire [7:0] DBUS, IMMED, RADDR, RF_Q, WR_q;
  wire [7:4] RFSRCR_q;
  wire [11:0] ADDRESS, MIPC;
  wire [15:0] pce_1_q;
  wire [47:44] DECODER_2_d;

  DCOUTER #(.generic("Bits := 12;")) dcouter_1 (
    .CLK(CLK_t), .nCLR(CLR), .CNT(1'b1), .nLE(DC_JUMP), .D(ADDRESS), .Q(MIPC));
  Comparator #(.Bits(8)) comparator_1 (
    .a(RF_Q), .b(IMMED), .gt(comparator_1_gt), .eq(comparator_1_eq), .lt(comparator_1_lt));
  Decoder #(.Selector_Bits(3)) decoder_1 (
    .sel(BUS_SRC), .out_0(ALUS_OE), .out_1(ALUDL_OE), .out_2(ALUDH_OE), .out_3(IMMED_OE), .out_4(RAM_OE),
    .out_5(XRAM_OE), .out_6(ROM_OE), .out_7(IRQ_OE));
  Multiplexer #(.Selector_Bits(3)) multiplexer_1 (
    .sel(JUMP_TYPE), .in_0(1'b0), .in_1(1'b1), .in_2(comparator_1_gt), .in_3(comparator_1_eq),
    .in_4(comparator_1_lt), .in_5(BR_Q), .in_6(RST), .in_7(1'b0), .out(DC_JUMP));
  PCE pce_1 (.CLK(CLK_t), .D(DBUS), .RS(RF_SRC), .LWE(RF_LWE), .HWE(RF_HWE), .Q(pce_1_q));
  ROM #(.AddrBits(12), .Bits(48)) DECODER_2 (
    .A(MIPC), .sel(1'b1),
    .D({DECODER_2_d, IMMED, ADDRESS, JUMP_TYPE, ALUSD_FUNC, RAM_WE, RFSRCR_WE, BR_SRC, SR_WE, WR_WE, BUS_SRC, RF_SFR, RF_HWE, RF_LWE, RF_SRC}));
  Register #(.Bits(8)) RFSRCR (.D(DBUS), .C(CLK_t), .en(RFSRCR_WE), .Q({RFSRCR_q, and_2_out[3:0]}));
  and and_1 (and_2_out[5], RFSRCR_q[4], RAM_WE);
  and and_2 (and_2_out[6], RFSRCR_q[4], RAM_OE);
  Comparator #(.Bits(12)) comparator_2 (.a(MIPCBI), .b(MIPC), .eq(comparator_2_eq));  // open: gt, lt
  Comparator #(.Bits(16)) comparator_3 (.a(PCBI), .b(pce_1_q), .eq(comparator_3_eq));  // open: gt, lt
  and and_3 (and_3_out, comparator_2_eq, MIPCBE);
  and and_4 (and_4_out, comparator_3_eq, PCBE);
  Multiplexer #(.Bits(7)) multiplexer_2 (
    .sel(RF_SFR), .in_0({1'b0, RF_HWE, RF_LWE, RF_SRC}),
    .in_1({and_2_out[6:5], and_2_out[5], and_2_out[3:0]}),
    .out({SFR_OE, multiplexer_2_out_2, multiplexer_2_out}));
  // Probe on MIPC
  // Probe on RF_SRC
  // Probe on RF_LWE
  // Probe on RF_HWE
  // Probe on RF_SFR
  // Probe on BUS_SRC
  // Probe on WR_WE
  // Probe on SR_WE
  // Probe on BR_SRC
  // Probe on RFSRCR_WE
  // Probe on RAM_WE
  // Probe on ALUSD_FUNC
  // Probe on JUMP_TYPE
  // Probe on ADDRESS
  // Probe on IMMED
  ASSERT ASSERT (.C(CLK_t), .D(DBUS), .A(RADDR), .WE(RAM_WE), .F(ASSERT_f));
  Button button_1 (.out(button_1_out));
  reg_file RF (
    .CLK(CLK_t), .RS(multiplexer_2_out), .D(DBUS), .LLE(multiplexer_2_out_2[4]),
    .HLE(multiplexer_2_out_2[5]), .Q(RF_Q));
  BR BR (.CLK(CLK_t), .CLR(CLR), .S(BR_SRC), .ALUDF(ALUD_CO), .ALUSF(ALUD_CO), .A0(RF_Q[0]), .A7(RF_Q[7]), .Q(BR_Q));
  or or_1 (or_1_out, ASSERT_f, and_3_out, and_4_out);
  // SwitchDT switchdt_1: pin names not known; wires that end beside it: clk, button_1_out, CLKR
  // Probe on RF_Q
  STALL STALL (.C(CLKR), .S(or_1_out), .G(in_4), .O(CLK_t));
  reg__sync_clear #(.generic("Bits := 8;")) WR (.D(DBUS), .CLK(CLK_t), .CLR(CLR), .nLE(WR_WE), .Q(WR_q));
  reg__sync_clear #(.generic("Bits := 8;")) SR (.D(DBUS), .CLK(CLK_t), .CLR(CLR), .nLE(SR_WE), .Q(RADDR));
  not not_1 (not_1_out, CLK_t);
  PullDown #(.Bits(8)) pulldown_1 (.out(DBUS));
  assign DBUS = SFR_OE ? RF_Q : 8'bz;  // Driver driver_1
  // Probe on WR_q
  // Probe on RADDR
  and and_5 (and_5_out, RAM_WE, CLK_t, not_1_out);
  // Probe on DBUS
  ALU ALU (
    .A(RF_Q), .B(WR_q), .S(ALUSD_FUNC), .CI(BR_Q), .nSOE(ALUS_OE), .nDLOE(ALUDL_OE), .nDHOE(ALUDH_OE),
    .O(DBUS), .CO(ALUD_CO));
  // Probe on {RADDR, WR_q}
  ROM #(.AddrBits(16), .Bits(8)) ROM (.A({RADDR, WR_q}), .sel(ROM_OE), .D(DBUS));
  RAMSinglePortSel #(.AddrBits(7), .isProgramMemory("true"), .Bits(8)) RAM (
    .A(RADDR[6:0]), .CS(~RADDR[7]), .WE(and_5_out), .OE(RAM_OE), .D(DBUS));
  // EXTCTL EXT: pin names not known; wires that end beside it: RAM_WE, RADDR, DBUS, CLK_t, EXT_p5
  // DUMP DUMP: pin names not known; wires that end beside it: RAM_WE, RADDR, DBUS, CLK_t, DUMP_p5
  // Probe on EXT_p5
  assign DBUS = IMMED_OE ? IMMED : 8'bz;  // Driver driver_2
  // Probe on DUMP_p5

  // Other names for the same wires on the sheet: GO = in_4

  // Notes on the sheet:
  //   clk: Hz: 2147483647
  //   contents of DECODER_2 (hex, n*v repeats v):
  //   12fc80488,80889,33a,85106,1c3135,1e54b8,1e08b9,8008c80000a,c004480000a,e002580000a,
  //   f001680000a,f801080040a,a00bc,80485,1a088c,236,f401380000a,f601280000a,f501380000a,
  //   f201580000a,f301580000a,f101680000a,e801e80000a,ec01b80000a,ee01a80000a,ef01a80000a,
  //   ed01b80000a,ea01d80000a,eb01d80000a,e901e80000a,e402280000a,e602180000a,e702180000a,
  //   e502280000a,e202480000a,e302480000a,e102580000a,d003580000a,d802e80000a,dc02b80000a,
  //   de02a80000a,df02a80000a,dd02b80000a,da02d80000a,db02d80000a,d902e80000a,d403280000a,
  //   d603180000a,d703180000a,d503280000a,d203480000a,d303480000a,d103580000a,c803d80000a,
  //   cc03a80000a,ce03980000a,cf03980000a,cd03a80000a,ca03c80000a,cb03c80000a,c903d80000a,
  //   c404180000a,c604080000a,c704080000a,c504180000a,c204380000a,c304380000a,c104480000a,
  //   a006780000a,b005580000a,b804e80000a,bc04b80000a,be04a80000a,bf04a80000a,bd04b80000a,
  //   ba04d80000a,bb04d80000a,b904e80000a,b405280000a,b605180000a,b705180000a,b505280000a,
  //   b205480000a,b305480000a,b105580000a,a805d80000a,ac05a80000a,ae05980000a,af05980000a,
  //   ad05a80000a,aa05c80000a,ab05c80000a,a905d80000a,a406180000a,a606080000a,a706080000a,
  //   a506180000a,a206680000a,a306680000a,3580,450b1,1172400b2,a106780000a,9006f80000a,
  //   9806980000a,9406c80000a,9606b80000a,9506c80000a,9206e80000a,9306e80000a,9106f80000a,
  //   8807780000a,8c07480000a,8e07380000a,8f07380000a,8d07480000a,8a07680000a,8b07680000a,
  //   8907780000a,8408980000a,8607a80000a,8707a80000a,8508980000a,fd000000980,10000,b3c,
  //   6800c,640,a30bd,1e54b8,1e08b9,8048d,b3c,6800c,b30c0,1e54b8,1173e08b9,8208b80000a,
  //   8308b80000a,8108c80000a,400d580000a,600b680000a,700a780000a,7809780000a,7c09480000a,
  //   7e09380000a,7f09380000a,7d09480000a,7a09680000a,7b09680000a,7909780000a,740a480000a,
  //   7609a80000a,7709a80000a,750a480000a,333c,1e54b8,1e08b9,700,6800c,8088c,b30c0,1e50b8,
  //   1173e00b9,720a680000a,730a680000a,710a780000a,680af80000a,6c0ac80000a,6e0ab80000a,
  //   6f0ab80000a,6d0ac80000a,6a0ae80000a,6b0ae80000a,690af80000a,640b380000a,660b280000a,
  //   670b280000a,650b380000a,620b580000a,630b580000a,610b680000a,500c680000a,580bf80000a,
  //   5c0bc80000a,5e0bb80000a,5f0bb80000a,5d0bc80000a,5a0be80000a,5b0be80000a,590bf80000a,
  //   540c380000a,560c280000a,570c280000a,550c380000a,520c580000a,530c580000a,510c680000a,
  //   480ce80000a,4c0cb80000a,4e0ca80000a,4f0ca80000a,4d0cb80000a,4a0cd80000a,4b0cd80000a,
  //   490ce80000a,440d280000a,460d180000a,470d180000a,450d280000a,420d480000a,430d480000a,
  //   410d580000a,200f580000a,300e680000a,380df80000a,3c0dc80000a,3e0db80000a,3f0db80000a,
  //   3d0dc80000a,3a0de80000a,3b0de80000a,390df80000a,340e380000a,360e280000a,370e280000a,
  //   350e380000a,320e580000a,330e580000a,310e680000a,280ee80000a,2c0eb80000a,2e0ea80000a,
  //   2f0ea80000a,2d0eb80000a,2a0ed80000a,2b0ed80000a,290ee80000a,240f280000a,260f180000a,
  //   270f180000a,250f280000a,220f480000a,230f480000a,210f580000a,1010580000a,180fe80000a,
  //   1c0fb80000a,1e0fa80000a,1f0fa80000a,1d0fb80000a,1a0fd80000a,1b0fd80000a,190fe80000a,
  //   1410280000a,1610180000a,1710180000a,1510280000a,1210480000a,1310480000a,1110580000a,
  //   810d80000a,c10a80000a,e10980000a,f10980000a,d10a80000a,a10c80000a,b10c80000a,910d80000a,
  //   411280000a,611080000a,711080000a,511180000a,100036,211580000a,311580000a,80036,111780000a,
  //   117200000,80000880483,3bc,e04bc,100080000c,80484,1600bc,8048b,a00bd,a00be,80484,16348d,
  //   6508c,a00000,10048c,e00be,40000e,c00bb,100830,90088,100830,90089,2043c,1b9,2a00b8,
  //   1b6,1b7,1b0,1b5,1b1,1b2,1b3,1b4,1b8,1b9,1ba,12fc001bb,200000
  //   contents of ROM (hex, n*v repeats v):
  //   75,0,0,75,1,1,75,2,2,75,3,3,75,4,4,75,5,5,75,6,6,75,7,7,75,8,8,75,9,9,75,a,a,75,b,
  //   b,75,c,c,75,d,d,75,e,e,75,f,f,75,10,10,75,11,11,75,12,12,75,13,13,75,14,14,75,15,
  //   15,75,16,16,75,17,17,75,18,18,75,19,19,75,1a,1a,75,1b,1b,75,1c,1c,75,1d,1d,75,1e,
  //   1e,75,1f,1f,75,20,20,75,21,21,75,22,22,75,23,23,75,24,24,75,25,25,75,26,26,75,27,
  //   27,75,28,28,75,29,29,75,2a,2a,75,2b,2b,75,2c,2c,75,2d,2d,75,2e,2e,75,2f,2f,75,30,
  //   30,75,31,31,75,32,32,75,33,33,75,34,34,75,35,35,75,36,36,75,37,37,75,38,38,75,39,
  //   39,75,3a,3a,75,3b,3b,75,3c,3c,75,3d,3d,75,3e,3e,75,3f,3f,75,40,40,75,41,41,75,42,
  //   42,75,43,43,75,44,44,75,45,45,75,46,46,75,47,47,75,48,48,75,49,49,75,4a,4a,75,4b,
  //   4b,75,4c,4c,75,4d,4d,75,4e,4e,75,4f,4f,75,50,50,75,51,51,75,52,52,75,53,53,75,54,
  //   54,75,55,55,75,56,56,75,57,57,75,58,58,75,59,59,75,5a,5a,75,5b,5b,75,5c,5c,75,5d,
  //   5d,75,5e,5e,75,5f,5f,75,60,60,75,61,61,75,62,62,75,63,63,75,64,64,75,65,65,75,66,
  //   66,75,67,67,75,68,68,75,69,69,75,6a,6a,75,6b,6b,75,6c,6c,75,6d,6d,75,6e,6e,75,6f,
  //   6f,75,70,70,75,71,71,75,72,72,75,73,73,75,74,74,75,75,75,75,76,76,75,77,77,75,78,
  //   78,75,79,79,75,7a,7a,75,7b,7b,75,7c,7c,75,7d,7d,75,7e,7e,75,7f,7f,75,0,0,75,1,1,75,
  //   2,2,75,3,3,75,4,4,75,5,5,75,6,6,75,7,7,75,8,8,75,9,9,75,a,a,75,b,b,75,c,c,75,d,d,
  //   75,e,e,75,f,f,75,10,10,75,11,11,75,12,12,75,13,13,75,14,14,75,15,15,75,16,16,75,17,
  //   17,75,18,18,75,19,19,75,1a,1a,75,1b,1b,75,1c,1c,75,1d,1d,75,1e,1e,75,1f,1f,75,20,
  //   20,75,21,21,75,22,22,75,23,23,75,24,24,75,25,25,75,26,26,75,27,27,75,28,28,75,29,
  //   29,75,2a,2a,75,2b,2b,75,2c,2c,75,2d,2d,75,2e,2e,75,2f,2f,75,30,30,75,31,31,75,32,
  //   32,75,33,33,75,34,34,75,35,35,75,36,36,75,37,37,75,38,38,75,39,39,75,3a,3a,75,3b,
  //   3b,75,3c,3c,75,3d,3d,75,3e,3e,75,3f,3f,75,40,40,75,41,41,75,42,42,75,43,43,75,44,
  //   44,75,45,45,75,46,46,75,47,47,75,48,48,75,49,49,75,4a,4a,75,4b,4b,75,4c,4c,75,4d,
  //   4d,75,4e,4e,75,4f,4f,75,50,50,75,51,51,75,52,52,75,53,53,75,54,54,75,55,55,75,56,
  //   56,75,57,57,75,58,58,75,59,59,75,5a,5a,75,5b,5b,75,5c,5c,75,5d,5d,75,5e,5e,75,5f,
  //   5f,75,60,60,75,61,61,75,62,62,75,63,63,75,64,64,75,65,65,75,66,66,75,67,67,75,68,
  //   68,75,69,69,75,6a,6a,75,6b,6b,75,6c,6c,75,6d,6d,75,6e,6e,75,6f,6f,75,70,70,75,71,
  //   71,75,72,72,75,73,73,75,74,74,75,75,75,75,76,76,75,77,77,75,78,78,75,79,79,75,7a,
  //   7a,75,7b,7b,75,7c,7c,75,7d,7d,75,7e,7e,75,7f,7f,75,81,81,75,82,82,75,83,83,75,a8,
  //   a8,75,b8,b8,75,d0,d0,75,e0,e0,75,f0,f0,85,0,0,85,1,1,85,2,2,85,3,3,85,4,4,85,5,5,
  //   85,6,6,85,7,7,85,8,8,85,9,9,85,a,a,85,b,b,85,c,c,85,d,d,85,e,e,85,f,f,85,10,10,85,
  //   11,11,85,12,12,85,13,13,85,14,14,85,15,15,85,16,16,85,17,17,85,18,18,85,19,19,85,
  //   1a,1a,85,1b,1b,85,1c,1c,85,1d,1d,85,1e,1e,85,1f,1f,85,20,20,85,21,21,85,22,22,85,
  //   23,23,85,24,24,85,25,25,85,26,26,85,27,27,85,28,28,85,29,29,85,2a,2a,85,2b,2b,85,
  //   2c,2c,85,2d,2d,85,2e,2e,85,2f,2f,85,30,30,85,31,31,85,32,32,85,33,33,85,34,34,85,
  //   35,35,85,36,36,85,37,37,85,38,38,85,39,39,85,3a,3a,85,3b,3b,85,3c,3c,85,3d,3d,85,
  //   3e,3e,85,3f,3f,85,40,40,85,41,41,85,42,42,85,43,43,85,44,44,85,45,45,85,46,46,85,
  //   47,47,85,48,48,85,49,49,85,4a,4a,85,4b,4b,85,4c,4c,85,4d,4d,85,4e,4e,85,4f,4f,85,
  //   50,50,85,51,51,85,52,52,85,53,53,85,54,54,85,55,55,85,56,56,85,57,57,85,58,58,85,
  //   59,59,85,5a,5a,85,5b,5b,85,5c,5c,85,5d,5d,85,5e,5e,85,5f,5f,85,60,60,85,61,61,85,
  //   62,62,85,63,63,85,64,64,85,65,65,85,66,66,85,67,67,85,68,68,85,69,69,85,6a,6a,85,
  //   6b,6b,85,6c,6c,85,6d,6d,85,6e,6e,85,6f,6f,85,70,70,85,71,71,85,72,72,85,73,73,85,
  //   74,74,85,75,75,85,76,76,85,77,77,85,78,78,85,79,79,85,7a,7a,85,7b,7b,85,7c,7c,85,
  //   7d,7d,85,7e,7e,85,7f,7f,85,0,0,85,1,1,85,2,2,85,3,3,85,4,4,85,5,5,85,6,6,85,7,7,85,
  //   8,8,85,9,9,85,a,a,85,b,b,85,c,c,85,d,d,85,e,e,85,f,f,85,10,10,85,11,11,85,12,12,85,
  //   13,13,85,14,14,85,15,15,85,16,16,85,17,17,85,18,18,85,19,19,85,1a,1a,85,1b,1b,85,
  //   1c,1c,85,1d,1d,85,1e,1e,85,1f,1f,85,20,20,85,21,21,85,22,22,85,23,23,85,24,24,85,
  //   25,25,85,26,26,85,27,27,85,28,28,85,29,29,85,2a,2a,85,2b,2b,85,2c,2c,85,2d,2d,85,
  //   2e,2e,85,2f,2f,85,30,30,85,31,31,85,32,32,85,33,33,85,34,34,85,35,35,85,36,36,85,
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endmodule
